// Logisim project 1607004_1607007_sap1.circ as structural Verilog: 17 circuits, main circuit main
module main (
  output [3:0] out_1,
  output [3:0] out_2
);

  wire CLK_out, controlled_buffer_1_out, Controller_Sequence_cp, Controller_Sequence_ea,
       Controller_Sequence_ep, Controller_Sequence_eu, Controller_Sequence_halt, Controller_Sequence_nce,
       Controller_Sequence_nei, Controller_Sequence_nla, Controller_Sequence_nlb, Controller_Sequence_nli,
       Controller_Sequence_nlm, Controller_Sequence_nlo, Controller_Sequence_su, not_1_out, not_2_out,
       RESET_out;
  wire [3:0] IR_to_sequencer, MAR_to_ram__y3_y2_y1_y0, Output_to_binary_display, Output_to_binary_display_2;
  wire [7:0] Accumulator_to_add_sub, B_register_to_add_sub;

  pc PC (
    .count(Controller_Sequence_cp), .To_bus__out(out_2), .clk(controlled_buffer_1_out), .clear(RESET_out),
    .Enable(Controller_Sequence_ep));
  MAR MAR (
    .from_bus__x3_x2_x1_x0(out_2), .nload(Controller_Sequence_nlm), .cp(controlled_buffer_1_out),
    .clr(RESET_out), .to_RAM__y3_y2_y1_y0(MAR_to_ram__y3_y2_y1_y0));
  not not_1 (not_1_out, Controller_Sequence_nce);
  ControllerSequencer Controller_Sequence (
    .CLK(controlled_buffer_1_out), .CLR(RESET_out), .I7(IR_to_sequencer[3]), ._16(IR_to_sequencer[2]),
    .I5(IR_to_sequencer[1]), .I4(IR_to_sequencer[0]), .Cp(Controller_Sequence_cp),
    .Ep(Controller_Sequence_ep), .nLm(Controller_Sequence_nlm), .nCE(Controller_Sequence_nce),
    .nLi(Controller_Sequence_nli), .nEi(Controller_Sequence_nei), .nLa(Controller_Sequence_nla),
    .Ea(Controller_Sequence_ea), .Su(Controller_Sequence_su), .Eu(Controller_Sequence_eu),
    .nLb(Controller_Sequence_nlb), .nLo(Controller_Sequence_nlo), .HALT(Controller_Sequence_halt));
  RAM #(.addrWidth(4), .bus("separate")) ram_1 (
    .addr(MAR_to_ram__y3_y2_y1_y0), .data({out_1, out_2}), .ld(not_1_out));  // open: din, str, sel, clk, clr
  IR IR (
    .From_Bus({out_1, out_2}), .nEa(Controller_Sequence_nei), .Li_prime(Controller_Sequence_nli),
    .CLK(controlled_buffer_1_out), .CLR(RESET_out), .To_Sequencer(IR_to_sequencer), .To_Bus(out_2));
  not not_2 (not_2_out, Controller_Sequence_halt);
  Clock CLK (.out(CLK_out));
  assign controlled_buffer_1_out = not_2_out ? CLK_out : 1'bz;  // Controlled_Buffer controlled_buffer_1
  Button RESET (.out(RESET_out));
  Accumulator Accumulator (
    .CLK(controlled_buffer_1_out), .CLR(RESET_out), .Ea(Controller_Sequence_ea), .From_Bus({out_1, out_2}),
    .nLa(Controller_Sequence_nla), .To_Bus({out_1, out_2}), .To_ADD_SUB(Accumulator_to_add_sub));
  Adder_Subtractor adder_subtractor_1 (
    .From_B_register(B_register_to_add_sub), .To_Bus({out_1, out_2}),
    .From_Accumulator(Accumulator_to_add_sub), .Su(Controller_Sequence_su), .Eu(Controller_Sequence_eu));
  B_Register B_register (
    .CLK(controlled_buffer_1_out), .CLR(RESET_out), .From_Bus({out_1, out_2}), .nLb(Controller_Sequence_nlb),
    .To_ADD_SUB(B_register_to_add_sub));
  Output_register Output (
    .CLK(controlled_buffer_1_out), .CLR(RESET_out), .From_Bus({out_1, out_2}), .nLo(Controller_Sequence_nlo),
    .To_Binary_Display({Output_to_binary_display_2, Output_to_binary_display}));
  Hex_Digit_Display hex_digit_display_1 (.value(Output_to_binary_display));  // open: dp
  Hex_Digit_Display hex_digit_display_2 (.value(Output_to_binary_display_2));  // open: dp

  // Notes on the sheet:
  //   1607004
  //   1607007
  //   1607007
endmodule

// A
module Accumulator (
  input  [7:0] From_Bus,
  input  nLa,
  input  CLK,
  input  CLR,
  input  Ea,
  output [7:0] To_Bus,
  output [7:0] To_ADD_SUB
);

  wire and_1_out, and_2_out, and_3_out, and_4_out, and_5_out, and_6_out, and_7_out, and_8_out, and_9_out,
       and_10_out, and_11_out, and_12_out, and_13_out, and_14_out, and_15_out, and_16_out, not_1_out,
       not_2_out, not_3_out, or_1_out, or_2_out, or_3_out, or_4_out, or_5_out, or_6_out, or_7_out, or_8_out;

  and and_1 (and_1_out, To_ADD_SUB[7], not_1_out);
  and and_2 (and_2_out, From_Bus[7], not_3_out);
  or or_1 (or_1_out, and_1_out, and_2_out);
  D_Flip_Flop d_ff_1 (.clk(CLK), .D(or_1_out), .Q(To_ADD_SUB[7]), .reset(CLR));  // open: Qn, preset, en
  and and_3 (and_3_out, To_ADD_SUB[6], not_1_out);
  assign To_Bus[7] = Ea ? To_ADD_SUB[7] : 1'bz;  // Controlled_Buffer controlled_buffer_1
  and and_4 (and_4_out, From_Bus[6], not_3_out);
  or or_2 (or_2_out, and_3_out, and_4_out);
  D_Flip_Flop d_ff_2 (.clk(CLK), .D(or_2_out), .Q(To_ADD_SUB[6]), .reset(CLR));  // open: Qn, preset, en
  assign To_Bus[6] = Ea ? To_ADD_SUB[6] : 1'bz;  // Controlled_Buffer controlled_buffer_2
  and and_5 (and_5_out, To_ADD_SUB[5], not_1_out);
  and and_6 (and_6_out, From_Bus[5], not_3_out);
  or or_3 (or_3_out, and_5_out, and_6_out);
  D_Flip_Flop d_ff_3 (.clk(CLK), .D(or_3_out), .Q(To_ADD_SUB[5]), .reset(CLR));  // open: Qn, preset, en
  assign To_Bus[5] = Ea ? To_ADD_SUB[5] : 1'bz;  // Controlled_Buffer controlled_buffer_3
  and and_7 (and_7_out, To_ADD_SUB[4], not_1_out);
  or or_4 (or_4_out, and_7_out, and_8_out);
  D_Flip_Flop d_ff_4 (.clk(CLK), .D(or_4_out), .Q(To_ADD_SUB[4]), .reset(CLR));  // open: Qn, preset, en
  assign To_Bus[4] = Ea ? To_ADD_SUB[4] : 1'bz;  // Controlled_Buffer controlled_buffer_4
  not not_1 (not_1_out, not_3_out);
  and and_8 (and_8_out, From_Bus[4], not_3_out);
  and and_9 (and_9_out, To_ADD_SUB[3], not_2_out);
  and and_10 (and_10_out, From_Bus[3], not_3_out);
  or or_5 (or_5_out, and_9_out, and_10_out);
  D_Flip_Flop d_ff_5 (.clk(CLK), .D(or_5_out), .Q(To_ADD_SUB[3]), .reset(CLR));  // open: Qn, preset, en
  assign To_Bus[3] = Ea ? To_ADD_SUB[3] : 1'bz;  // Controlled_Buffer controlled_buffer_5
  and and_11 (and_11_out, To_ADD_SUB[2], not_2_out);
  and and_12 (and_12_out, From_Bus[2], not_3_out);
  or or_6 (or_6_out, and_11_out, and_12_out);
  D_Flip_Flop d_ff_6 (.clk(CLK), .D(or_6_out), .Q(To_ADD_SUB[2]), .reset(CLR));  // open: Qn, preset, en
  assign To_Bus[2] = Ea ? To_ADD_SUB[2] : 1'bz;  // Controlled_Buffer controlled_buffer_6
  and and_13 (and_13_out, To_ADD_SUB[1], not_2_out);
  or or_7 (or_7_out, and_13_out, and_14_out);
  D_Flip_Flop d_ff_7 (.clk(CLK), .D(or_7_out), .Q(To_ADD_SUB[1]), .reset(CLR));  // open: Qn, preset, en
  assign To_Bus[1] = Ea ? To_ADD_SUB[1] : 1'bz;  // Controlled_Buffer controlled_buffer_7
  and and_14 (and_14_out, From_Bus[1], not_3_out);
  and and_15 (and_15_out, To_ADD_SUB[0], not_2_out);
  D_Flip_Flop d_ff_8 (.clk(CLK), .D(or_8_out), .Q(To_ADD_SUB[0]), .reset(CLR));  // open: Qn, preset, en
  assign To_Bus[0] = Ea ? To_ADD_SUB[0] : 1'bz;  // Controlled_Buffer controlled_buffer_8
  and and_16 (and_16_out, From_Bus[0], not_3_out);
  or or_8 (or_8_out, and_15_out, and_16_out);
  not not_2 (not_2_out, not_3_out);
  not not_3 (not_3_out, nLa);

  // Notes on the sheet:
  //   Ea: pull=up
  //   1607007
  //   1607007
endmodule

// FA
module Full_adder (
  input  A,
  input  B,
  input  Cin,
  output Sum,
  output Cout
);

  wire and_1_out, and_2_out, xor_1_out;

  xor xor_1 (xor_1_out, A, B);
  and and_1 (and_1_out, A, B);
  xor xor_2 (Sum, xor_1_out, Cin);
  and and_2 (and_2_out, xor_1_out, Cin);
  or or_1 (Cout, and_2_out, and_1_out);
  // NOT_Gate not_1 is placed but not wired
  // NOT_Gate not_2 is placed but not wired

  // Notes on the sheet:
  //   1607007
endmodule

module half_adder (
  input  A,
  input  B,
  output Sum,
  output Carry
);

  xor xor_1 (Sum, A, B);
  and and_1 (Carry, B, A);

  // Notes on the sheet:
  //   1607007
endmodule

// ADD-SUB
module Adder_Subtractor (
  input  [7:0] From_B_register,
  input  Su,
  input  Eu,
  input  [7:0] From_Accumulator,
  output [7:0] To_Bus
);

  wire full_adder_2_cout, full_adder_3_cout, full_adder_4_cout, full_adder_5_cout, full_adder_6_cout,
       full_adder_7_cout, full_adder_8_cout, xor_1_out, xor_2_out, xor_3_out, xor_4_out, xor_5_out,
       xor_6_out, xor_7_out, xor_8_out;
  wire [7:0] full_adder_8_sum;

  assign To_Bus = Eu ? full_adder_8_sum : 8'bz;  // Controlled_Buffer controlled_buffer_1
  Full_adder full_adder_1 (
    .A(From_Accumulator[7]), .B(xor_1_out), .Cin(full_adder_2_cout), .Sum(full_adder_8_sum[7]));  // open: Cout
  xor xor_1 (xor_1_out, Su, From_B_register[7]);
  Full_adder full_adder_2 (
    .A(From_Accumulator[6]), .B(xor_2_out), .Cin(full_adder_3_cout), .Sum(full_adder_8_sum[6]),
    .Cout(full_adder_2_cout));
  xor xor_2 (xor_2_out, Su, From_B_register[6]);
  Full_adder full_adder_3 (
    .A(From_Accumulator[5]), .B(xor_3_out), .Cin(full_adder_4_cout), .Sum(full_adder_8_sum[5]),
    .Cout(full_adder_3_cout));
  xor xor_3 (xor_3_out, Su, From_B_register[5]);
  Full_adder full_adder_4 (
    .A(From_Accumulator[4]), .B(xor_5_out), .Cin(full_adder_5_cout), .Sum(full_adder_8_sum[4]),
    .Cout(full_adder_4_cout));
  xor xor_4 (xor_4_out, Su, From_B_register[3]);
  xor xor_5 (xor_5_out, Su, From_B_register[4]);
  Full_adder full_adder_5 (
    .A(From_Accumulator[3]), .B(xor_4_out), .Cin(full_adder_6_cout), .Sum(full_adder_8_sum[3]),
    .Cout(full_adder_5_cout));
  xor xor_6 (xor_6_out, Su, From_B_register[2]);
  Full_adder full_adder_6 (
    .A(From_Accumulator[2]), .B(xor_6_out), .Cin(full_adder_7_cout), .Sum(full_adder_8_sum[2]),
    .Cout(full_adder_6_cout));
  xor xor_7 (xor_7_out, Su, From_B_register[1]);
  Full_adder full_adder_7 (
    .A(From_Accumulator[1]), .B(xor_7_out), .Cin(full_adder_8_cout), .Sum(full_adder_8_sum[1]),
    .Cout(full_adder_7_cout));
  xor xor_8 (xor_8_out, Su, From_B_register[0]);
  Full_adder full_adder_8 (
    .A(From_Accumulator[0]), .B(xor_8_out), .Cin(Su), .Sum(full_adder_8_sum[0]), .Cout(full_adder_8_cout));

  // Notes on the sheet:
  //   1607007
endmodule

// B
module B_Register (
  input  [7:0] From_Bus,
  input  nLb,
  input  CLK,
  input  CLR,
  output [7:0] To_ADD_SUB
);

  wire and_1_out, and_2_out, and_3_out, and_4_out, and_5_out, and_6_out, and_7_out, and_8_out, and_9_out,
       and_10_out, and_11_out, and_12_out, and_13_out, and_14_out, and_15_out, and_16_out, not_1_out,
       not_2_out, not_3_out, or_1_out, or_2_out, or_3_out, or_4_out, or_5_out, or_6_out, or_7_out, or_8_out;

  and and_1 (and_1_out, To_ADD_SUB[7], not_1_out);
  and and_2 (and_2_out, From_Bus[7], not_3_out);
  or or_1 (or_1_out, and_1_out, and_2_out);
  D_Flip_Flop d_ff_1 (.clk(CLK), .D(or_1_out), .Q(To_ADD_SUB[7]), .reset(CLR));  // open: Qn, preset, en
  and and_3 (and_3_out, To_ADD_SUB[6], not_1_out);
  and and_4 (and_4_out, From_Bus[6], not_3_out);
  or or_2 (or_2_out, and_3_out, and_4_out);
  D_Flip_Flop d_ff_2 (.clk(CLK), .D(or_2_out), .Q(To_ADD_SUB[6]), .reset(CLR));  // open: Qn, preset, en
  and and_5 (and_5_out, From_Bus[5], not_3_out);
  and and_6 (and_6_out, To_ADD_SUB[5], not_1_out);
  or or_3 (or_3_out, and_6_out, and_5_out);
  D_Flip_Flop d_ff_3 (.clk(CLK), .D(or_3_out), .Q(To_ADD_SUB[5]), .reset(CLR));  // open: Qn, preset, en
  and and_7 (and_7_out, To_ADD_SUB[4], not_1_out);
  or or_4 (or_4_out, and_7_out, and_8_out);
  D_Flip_Flop d_ff_4 (.clk(CLK), .D(or_4_out), .Q(To_ADD_SUB[4]), .reset(CLR));  // open: Qn, preset, en
  not not_1 (not_1_out, not_3_out);
  and and_8 (and_8_out, From_Bus[4], not_3_out);
  and and_9 (and_9_out, To_ADD_SUB[3], not_2_out);
  and and_10 (and_10_out, From_Bus[3], not_3_out);
  or or_5 (or_5_out, and_9_out, and_10_out);
  D_Flip_Flop d_ff_5 (.clk(CLK), .D(or_5_out), .Q(To_ADD_SUB[3]), .reset(CLR));  // open: Qn, preset, en
  and and_11 (and_11_out, To_ADD_SUB[2], not_2_out);
  and and_12 (and_12_out, From_Bus[2], not_3_out);
  or or_6 (or_6_out, and_11_out, and_12_out);
  D_Flip_Flop d_ff_6 (.clk(CLK), .D(or_6_out), .Q(To_ADD_SUB[2]), .reset(CLR));  // open: Qn, preset, en
  and and_13 (and_13_out, To_ADD_SUB[1], not_2_out);
  or or_7 (or_7_out, and_13_out, and_14_out);
  D_Flip_Flop d_ff_7 (.clk(CLK), .D(or_7_out), .Q(To_ADD_SUB[1]), .reset(CLR));  // open: Qn, preset, en
  and and_14 (and_14_out, From_Bus[1], not_3_out);
  and and_15 (and_15_out, To_ADD_SUB[0], not_2_out);
  D_Flip_Flop d_ff_8 (.clk(CLK), .D(or_8_out), .Q(To_ADD_SUB[0]), .reset(CLR));  // open: Qn, preset, en
  and and_16 (and_16_out, From_Bus[0], not_3_out);
  or or_8 (or_8_out, and_15_out, and_16_out);
  not not_2 (not_2_out, not_3_out);
  not not_3 (not_3_out, nLb);

  // Notes on the sheet:
  //   1607007
  //   1607007
endmodule

// Output
module Output_register (
  input  [7:0] From_Bus,
  input  nLo,
  input  CLK,
  input  CLR,
  output [7:0] To_Binary_Display
);

  wire and_1_out, and_2_out, and_3_out, and_4_out, and_5_out, and_6_out, and_7_out, and_8_out, and_9_out,
       and_10_out, and_11_out, and_12_out, and_13_out, and_14_out, and_15_out, and_16_out, not_1_out,
       not_2_out, not_3_out, or_1_out, or_2_out, or_3_out, or_4_out, or_5_out, or_6_out, or_7_out, or_8_out;

  and and_1 (and_1_out, To_Binary_Display[7], not_1_out);
  and and_2 (and_2_out, From_Bus[7], not_3_out);
  or or_1 (or_1_out, and_1_out, and_2_out);
  D_Flip_Flop d_ff_1 (.clk(CLK), .D(or_1_out), .Q(To_Binary_Display[7]), .reset(CLR));  // open: Qn, preset, en
  and and_3 (and_3_out, To_Binary_Display[6], not_1_out);
  and and_4 (and_4_out, From_Bus[6], not_3_out);
  or or_2 (or_2_out, and_3_out, and_4_out);
  D_Flip_Flop d_ff_2 (.clk(CLK), .D(or_2_out), .Q(To_Binary_Display[6]), .reset(CLR));  // open: Qn, preset, en
  and and_5 (and_5_out, To_Binary_Display[5], not_1_out);
  and and_6 (and_6_out, From_Bus[5], not_3_out);
  or or_3 (or_3_out, and_5_out, and_6_out);
  D_Flip_Flop d_ff_3 (.clk(CLK), .D(or_3_out), .Q(To_Binary_Display[5]), .reset(CLR));  // open: Qn, preset, en
  and and_7 (and_7_out, To_Binary_Display[4], not_1_out);
  or or_4 (or_4_out, and_7_out, and_8_out);
  D_Flip_Flop d_ff_4 (.clk(CLK), .D(or_4_out), .Q(To_Binary_Display[4]), .reset(CLR));  // open: Qn, preset, en
  not not_1 (not_1_out, not_3_out);
  and and_8 (and_8_out, From_Bus[4], not_3_out);
  and and_9 (and_9_out, To_Binary_Display[3], not_2_out);
  and and_10 (and_10_out, From_Bus[3], not_3_out);
  or or_5 (or_5_out, and_9_out, and_10_out);
  D_Flip_Flop d_ff_5 (.clk(CLK), .D(or_5_out), .Q(To_Binary_Display[3]), .reset(CLR));  // open: Qn, preset, en
  and and_11 (and_11_out, From_Bus[2], not_3_out);
  and and_12 (and_12_out, To_Binary_Display[2], not_2_out);
  or or_6 (or_6_out, and_12_out, and_11_out);
  D_Flip_Flop d_ff_6 (.clk(CLK), .D(or_6_out), .Q(To_Binary_Display[2]), .reset(CLR));  // open: Qn, preset, en
  and and_13 (and_13_out, To_Binary_Display[1], not_2_out);
  or or_7 (or_7_out, and_13_out, and_14_out);
  D_Flip_Flop d_ff_7 (.clk(CLK), .D(or_7_out), .Q(To_Binary_Display[1]), .reset(CLR));  // open: Qn, preset, en
  and and_14 (and_14_out, From_Bus[1], not_3_out);
  and and_15 (and_15_out, To_Binary_Display[0], not_2_out);
  D_Flip_Flop d_ff_8 (.clk(CLK), .D(or_8_out), .Q(To_Binary_Display[0]), .reset(CLR));  // open: Qn, preset, en
  and and_16 (and_16_out, From_Bus[0], not_3_out);
  or or_8 (or_8_out, and_15_out, and_16_out);
  not not_2 (not_2_out, not_3_out);
  not not_3 (not_3_out, nLo);

  // Notes on the sheet:
  //   1607007
  //   1607007
endmodule

module pc (
  input  count,
  input  clk,
  input  clear,
  input  Enable,
  output [3:0] To_bus__out
);

  wire and_1_out, and_2_out, and_3_out, j_k_ff_1_q, j_k_ff_2_q, j_k_ff_3_q, j_k_ff_4_q;

  and and_1 (and_1_out, count, j_k_ff_2_q, and_2_out);
  J_K_Flip_Flop j_k_ff_1 (
    .J(and_1_out), .clk(clk), .K(and_1_out), .Q(j_k_ff_1_q), .reset(clear));  // open: Qn, preset, en
  assign To_bus__out[3] = Enable ? j_k_ff_1_q : 1'bz;  // Controlled_Buffer controlled_buffer_1
  and and_2 (and_2_out, count, j_k_ff_3_q, and_3_out);
  J_K_Flip_Flop j_k_ff_2 (
    .J(and_2_out), .clk(clk), .K(and_2_out), .Q(j_k_ff_2_q), .reset(clear));  // open: Qn, preset, en
  assign To_bus__out[2] = Enable ? j_k_ff_2_q : 1'bz;  // Controlled_Buffer controlled_buffer_2
  and and_3 (and_3_out, count, j_k_ff_4_q);
  J_K_Flip_Flop j_k_ff_3 (
    .J(and_3_out), .clk(clk), .K(and_3_out), .Q(j_k_ff_3_q), .reset(clear));  // open: Qn, preset, en
  assign To_bus__out[1] = Enable ? j_k_ff_3_q : 1'bz;  // Controlled_Buffer controlled_buffer_3
  J_K_Flip_Flop j_k_ff_4 (.J(count), .clk(clk), .K(count), .Q(j_k_ff_4_q), .reset(clear));  // open: Qn, preset, en
  assign To_bus__out[0] = Enable ? j_k_ff_4_q : 1'bz;  // Controlled_Buffer controlled_buffer_4

  // Notes on the sheet:
  //   program counter
  //   roll-1607004
endmodule

module cir1 (
  input  load,
  input  x,
  input  a,
  output D
);

  wire and_1_out, and_2_out, not_1_out;

  not not_1 (not_1_out, load);
  and and_1 (and_1_out, load, x);
  and and_2 (and_2_out, not_1_out, a);
  or or_1 (D, and_1_out, and_2_out);

  // Notes on the sheet:
  //   sub circuit of register
  //   roll-1607004
endmodule

// 4 bit reg
module _4bit_reg (
  input  X3,
  input  X2,
  input  X1,
  input  X0,
  input  Load,
  input  clock_pulse,
  input  clear,
  input  Ea,
  output Y3,
  output Y2,
  output Y1,
  output Y0
);

  wire and_1_out, and_2_out, and_3_out, and_4_out, and_5_out, and_6_out, and_7_out, and_8_out, d_ff_1_q,
       d_ff_2_q, d_ff_3_q, d_ff_4_q, not_1_out, or_1_out, or_2_out, or_3_out, or_4_out;

  and and_1 (and_1_out, d_ff_1_q, not_1_out);
  or or_1 (or_1_out, and_1_out, and_2_out);
  and and_2 (and_2_out, X3, Load);
  D_Flip_Flop d_ff_1 (.clk(clock_pulse), .D(or_1_out), .Q(d_ff_1_q), .reset(clear));  // open: Qn, preset, en
  assign Y3 = Ea ? d_ff_1_q : 1'bz;  // Controlled_Buffer controlled_buffer_1
  and and_3 (and_3_out, d_ff_2_q, not_1_out);
  or or_2 (or_2_out, and_3_out, and_4_out);
  D_Flip_Flop d_ff_2 (.clk(clock_pulse), .D(or_2_out), .Q(d_ff_2_q), .reset(clear));  // open: Qn, preset, en
  and and_4 (and_4_out, X2, Load);
  assign Y2 = Ea ? d_ff_2_q : 1'bz;  // Controlled_Buffer controlled_buffer_2
  and and_5 (and_5_out, d_ff_3_q, not_1_out);
  D_Flip_Flop d_ff_3 (.clk(clock_pulse), .D(or_3_out), .Q(d_ff_3_q), .reset(clear));  // open: Qn, preset, en
  and and_6 (and_6_out, X1, Load);
  or or_3 (or_3_out, and_5_out, and_6_out);
  assign Y1 = Ea ? d_ff_3_q : 1'bz;  // Controlled_Buffer controlled_buffer_3
  D_Flip_Flop d_ff_4 (.clk(clock_pulse), .D(or_4_out), .Q(d_ff_4_q), .reset(clear));  // open: Qn, preset, en
  and and_7 (and_7_out, d_ff_4_q, not_1_out);
  and and_8 (and_8_out, X0, Load);
  or or_4 (or_4_out, and_7_out, and_8_out);
  assign Y0 = Ea ? d_ff_4_q : 1'bz;  // Controlled_Buffer controlled_buffer_4
  not not_1 (not_1_out, Load);

  // Notes on the sheet:
  //   4 bit register
  //   roll-1607004
  //   1607007
endmodule

module _8bit_reg (
  input  [3:0] x7_x6_x5_x4,
  input  load,
  input  cp,
  input  clr,
  input  [3:0] x3_x2_x1_x0,
  output y7,
  output y6,
  output y5,
  output y4,
  output y3,
  output y2,
  output y1,
  output y0
);

  // _4bit_reg 4bit_reg_1: pin names not known; wires that end beside it: x7_x6_x5_x4[3], x7_x6_x5_x4[2], x7_x6_x5_x4[1], x7_x6_x5_x4[0], cp, clr, load, y7, y6, y5, y4
  // _4bit_reg 4bit_reg_2: pin names not known; wires that end beside it: y0, y1, y2, y3, load, clr, cp, x3_x2_x1_x0[0], x3_x2_x1_x0[1], x3_x2_x1_x0[2], x3_x2_x1_x0[3]

  // Notes on the sheet:
  //   8bit register 
  //   roll-1607004
endmodule

module IR (
  input  [7:0] From_Bus,
  input  nEa,
  input  Li_prime,
  input  CLK,
  input  CLR,
  output [3:0] To_Sequencer,
  output [3:0] To_Bus
);

  wire not_1_out, not_2_out;

  not not_1 (not_1_out, nEa);
  not not_2 (not_2_out, Li_prime);
  _4bit_reg u_4bit_reg_1 (
    .X3(From_Bus[3]), .X2(From_Bus[2]), .X1(From_Bus[1]), .X0(From_Bus[0]), .clock_pulse(CLK), .clear(CLR),
    .Ea(not_1_out), .Load(not_2_out), .Y3(To_Bus[3]), .Y2(To_Bus[2]), .Y1(To_Bus[1]), .Y0(To_Bus[0]));
  _4bit_reg u_4bit_reg_2 (
    .X3(From_Bus[7]), .X2(From_Bus[6]), .X1(From_Bus[5]), .X0(From_Bus[4]), .clock_pulse(CLK), .clear(CLR),
    .Ea(1'b1), .Load(not_2_out), .Y3(To_Sequencer[3]), .Y2(To_Sequencer[2]), .Y1(To_Sequencer[1]),
    .Y0(To_Sequencer[0]));

  // Notes on the sheet:
  //   Instruction Register
  //   roll-1607004
endmodule

module MAR (
  input  [3:0] from_bus__x3_x2_x1_x0,
  input  nload,
  input  cp,
  input  clr,
  output [3:0] to_RAM__y3_y2_y1_y0
);

  wire not_1_out;

  not not_1 (not_1_out, nload);
  _4bit_reg u_4bit_reg_1 (
    .X3(from_bus__x3_x2_x1_x0[3]), .X2(from_bus__x3_x2_x1_x0[2]), .X1(from_bus__x3_x2_x1_x0[1]),
    .X0(from_bus__x3_x2_x1_x0[0]), .clock_pulse(cp), .clear(clr), .Ea(1'b1), .Load(not_1_out),
    .Y3(to_RAM__y3_y2_y1_y0[3]), .Y2(to_RAM__y3_y2_y1_y0[2]), .Y1(to_RAM__y3_y2_y1_y0[1]),
    .Y0(to_RAM__y3_y2_y1_y0[0]));

  // Notes on the sheet:
  //   Memory Address Register
  //   roll-1607004
endmodule

module decoder (
  input  I7,
  input  I6,
  input  I5,
  input  I4,
  output LDA,
  output ADD,
  output SUB,
  output OUT,
  output HLT
);

  wire and_1_out, and_2_out, and_3_out, and_4_out, and_5_out, not_1_out, not_2_out, not_3_out, not_4_out;

  not not_1 (not_1_out, I7);
  not not_2 (not_2_out, I6);
  not not_3 (not_3_out, I5);
  not not_4 (not_4_out, I4);
  buf buffer_1 (LDA, and_1_out);
  and and_1 (and_1_out, not_1_out, not_2_out, not_3_out, not_4_out);
  and and_2 (and_2_out, not_1_out, not_2_out, not_3_out, I4);
  buf buffer_2 (ADD, and_2_out);
  buf buffer_3 (SUB, and_3_out);
  and and_3 (and_3_out, not_1_out, not_2_out, I5, not_4_out);
  buf buffer_4 (OUT, and_4_out);
  and and_4 (and_4_out, I7, I6, I5, not_4_out);
  and and_5 (and_5_out, I7, I6, I5, I4);
  buf buffer_5 (HLT, and_5_out);

  // Notes on the sheet:
  //   Decoder
  //   roll-1607004
endmodule

module ring_counter (
  input  CLK,
  input  CLR,
  output T1,
  output T2,
  output T3,
  output T4,
  output T5,
  output T6
);

  wire j_k_ff_1_q, j_k_ff_2_qn, j_k_ff_3_qn, j_k_ff_4_qn, j_k_ff_5_qn, j_k_ff_6_qn, not_1_out;

  not not_1 (not_1_out, CLK);
  J_K_Flip_Flop j_k_ff_1 (
    .J(j_k_ff_6_qn), .clk(not_1_out), .K(T6), .Q(j_k_ff_1_q), .Qn(T1), .reset(CLR));  // open: preset, en
  J_K_Flip_Flop j_k_ff_2 (
    .J(T1), .clk(not_1_out), .K(j_k_ff_1_q), .Q(T2), .Qn(j_k_ff_2_qn), .reset(CLR));  // open: preset, en
  J_K_Flip_Flop j_k_ff_3 (
    .J(T2), .clk(not_1_out), .K(j_k_ff_2_qn), .Q(T3), .Qn(j_k_ff_3_qn), .reset(CLR));  // open: preset, en
  J_K_Flip_Flop j_k_ff_4 (
    .J(T3), .clk(not_1_out), .K(j_k_ff_3_qn), .Q(T4), .Qn(j_k_ff_4_qn), .reset(CLR));  // open: preset, en
  J_K_Flip_Flop j_k_ff_5 (
    .J(T4), .clk(not_1_out), .K(j_k_ff_4_qn), .Q(T5), .Qn(j_k_ff_5_qn), .reset(CLR));  // open: preset, en
  J_K_Flip_Flop j_k_ff_6 (
    .J(T5), .clk(not_1_out), .K(j_k_ff_5_qn), .Q(T6), .Qn(j_k_ff_6_qn), .reset(CLR));  // open: preset, en

  // Notes on the sheet:
  //   Ring Counter
  //   roll-1607004
endmodule

module ControllerSequencer (
  input  CLK,
  input  CLR,
  input  I5,
  input  _16,
  input  I4,
  input  I7,
  output Cp,
  output Ep,
  output nLm,
  output nCE,
  output nLi,
  output nEi,
  output nLa,
  output Ea,
  output Su,
  output Eu,
  output nLb,
  output nLo,
  output HALT
);

  wire and_1_out, and_2_out, and_3_out, and_4_out, and_5_out, and_6_out, and_7_out, and_8_out, and_9_out,
       and_10_out, and_11_out, and_12_out, and_14_out, and_16_out, and_17_out, and_18_out, decoder_1_add,
       decoder_1_lda, decoder_1_out, decoder_1_sub, ring_counter_1_t3, ring_counter_1_t4, ring_counter_1_t5,
       ring_counter_1_t6;

  ring_counter ring_counter_1 (
    .CLK(CLK), .CLR(CLR), .T1(Ep), .T2(Cp), .T3(ring_counter_1_t3), .T4(ring_counter_1_t4),
    .T5(ring_counter_1_t5), .T6(ring_counter_1_t6));
  decoder decoder_1 (
    .I7(I7), .I6(_16), .I5(I5), .I4(I4), .LDA(decoder_1_lda), .ADD(decoder_1_add), .SUB(decoder_1_sub),
    .OUT(decoder_1_out), .HLT(HALT));
  and and_1 (and_1_out, ring_counter_1_t4, decoder_1_add);
  and and_2 (and_2_out, ring_counter_1_t4, decoder_1_lda);
  nor nor_1 (nLm, and_2_out, and_1_out, and_4_out, Ep);
  and and_3 (and_3_out, ring_counter_1_t5, decoder_1_lda);
  and and_4 (and_4_out, ring_counter_1_t4, decoder_1_sub);
  Hex_Digit_Display hex_digit_display_1 (.value({Cp, Ep, nLm, nCE}));  // open: dp
  and and_5 (and_5_out, decoder_1_sub, ring_counter_1_t5);
  and and_6 (and_6_out, decoder_1_add, ring_counter_1_t5);
  nor nor_2 (nCE, and_3_out, and_6_out, and_5_out, ring_counter_1_t3);
  and and_7 (and_7_out, ring_counter_1_t4, decoder_1_lda);
  not not_1 (nLi, ring_counter_1_t3);
  and and_8 (and_8_out, ring_counter_1_t4, decoder_1_add);
  and and_9 (and_9_out, ring_counter_1_t4, decoder_1_sub);
  nor nor_3 (nEi, and_7_out, and_8_out, and_9_out);
  and and_10 (and_10_out, decoder_1_add, ring_counter_1_t6);
  and and_11 (and_11_out, ring_counter_1_t5, decoder_1_lda);
  nor nor_4 (nLa, and_11_out, and_10_out, and_12_out);
  Hex_Digit_Display hex_digit_display_2 (.value({nLi, nEi, nLa, Ea}));  // open: dp
  and and_12 (and_12_out, decoder_1_sub, ring_counter_1_t6);
  and and_13 (Ea, ring_counter_1_t4, decoder_1_out);
  and and_14 (and_14_out, ring_counter_1_t6, decoder_1_add);
  and and_15 (Su, ring_counter_1_t6, decoder_1_sub);
  or or_1 (Eu, and_14_out, and_16_out);
  and and_16 (and_16_out, ring_counter_1_t6, decoder_1_sub);
  and and_17 (and_17_out, ring_counter_1_t5, decoder_1_add);
  nor nor_5 (nLb, and_17_out, and_18_out);
  and and_18 (and_18_out, ring_counter_1_t5, decoder_1_sub);
  nand nand_1 (nLo, decoder_1_out, ring_counter_1_t4);
  Hex_Digit_Display hex_digit_display_3 (.value({Su, Eu, nLb, nLo}));  // open: dp

  // Notes on the sheet:
  //   1607007& 1607004
endmodule

module mulitplexur (
  input  [3:0] in_1,
  input  [3:0] in_2,
  input  in_3,
  output [3:0] out_4
);

  Multiplexer #(.width(4)) multiplexer_1 (.in0(in_1), .in1(in_2), .out(out_4), .sel(in_3));  // open: en
endmodule
